// Logisim project SC.circ as structural Verilog: 6 circuits, main circuit main
module main (
  input  in_1
);

  wire and_1_out, and_2_out, and_3_out, AND_4_out, clock_1_out, dec_1_addzero, dec_1_grzero, dec_1_inple,
       dec_1_memlb, dec_1_refmem, dec_1_sine, dec_1_zero, not_1_out, not_2_out, not_3_out, OR2_out, or_1_out,
       or_2_out, PC_carry, sc_1_out_3, sc_1_out_4, sc_1_out_5, sc_1_out_6;
  wire [1:0] compare_1_out_2, priority_encoder_1_out, priority_encoder_2_out, register_5_q;
  wire [3:0] alu_1_out_3, AR_q, IR_q, multiplexer_1_out, multiplexer_2_out, multiplexer_3_out,
       outple_1_out_8, outple_1_out_9, PC_q, ram_1_data, register_1_q, register_2_q, register_3_q,
       register_4_q, RS_q;

  Clock clock_1 (.out(clock_1_out));
  Counter #(.width(4), .max('hf), .trigger("falling")) PC (
    .load(or_1_out), .D(ram_1_data), .count(1'b1), .Q(PC_q), .carry(PC_carry), .clk(AND_4_out), .clr(in_1));
  or OR2 (OR2_out, PC_carry, in_1);
  SC sc_1 (
    .CLK(clock_1_out), .RST(OR2_out), .out_3(sc_1_out_3), .out_4(sc_1_out_4), .out_5(sc_1_out_5),
    .out_6(sc_1_out_6));
  or or_1 (or_1_out, and_1_out, and_2_out);
  and and_1 (and_1_out, register_5_q[0], dec_1_sine);
  and and_2 (and_2_out, register_5_q[1], dec_1_zero);
  or or_2 (or_2_out, sc_1_out_5, sc_1_out_6);
  Multiplexer #(.width(4), .enable("false")) multiplexer_1 (
    .in0(PC_q), .in1(AR_q), .out(multiplexer_1_out), .sel(and_3_out));
  and and_3 (and_3_out, dec_1_refmem, sc_1_out_6);
  Register #(.width(4)) AR (.D(ram_1_data), .en(sc_1_out_5), .Q(AR_q), .clk(clock_1_out), .clr(in_1));
  dec dec_1 (
    .in_1(IR_q), .sine(dec_1_sine), .zero(dec_1_zero), .INple(dec_1_inple), .addZERO(dec_1_addzero),
    .GRZERO(dec_1_grzero), .MEMlb(dec_1_memlb), .refMEM(dec_1_refmem));
  Register #(.width(4)) IR (.D(ram_1_data), .en(sc_1_out_3), .Q(IR_q), .clk(clock_1_out), .clr(in_1));
  Register #(.width(4)) RS (.D(ram_1_data), .en(sc_1_out_4), .Q(RS_q), .clk(clock_1_out), .clr(in_1));
  not not_1 (not_1_out, or_2_out);
  Multiplexer #(.width(4), .enable("false")) multiplexer_2 (
    .in0(ram_1_data), .in1(alu_1_out_3), .out(multiplexer_2_out), .sel(dec_1_inple));
  RAM #(.addrWidth(4), .dataWidth(4)) ram_1 (
    .addr(multiplexer_1_out), .data(ram_1_data), .clk(clock_1_out), .ld(not_2_out));  // open: sel, clr
  not not_2 (not_2_out, dec_1_memlb);
  Multiplexer #(.width(4), .enable("false")) multiplexer_3 (
    .in0(RS_q), .in1(4'b0000), .out(multiplexer_3_out), .sel(not_3_out));
  not not_3 (not_3_out, dec_1_grzero);
  and AND_4 (AND_4_out, not_1_out, clock_1_out);
  Priority_Encoder #(.select(2)) priority_encoder_1 (
    .in0(multiplexer_3_out[0]), .in1(multiplexer_3_out[1]), .in2(multiplexer_3_out[2]),
    .in3(multiplexer_3_out[3]), .out(priority_encoder_1_out));  // open: gs, en_out, en_in
  Priority_Encoder #(.select(2)) priority_encoder_2 (
    .in0(ram_1_data[0]), .in1(ram_1_data[1]), .in2(ram_1_data[2]), .in3(ram_1_data[3]),
    .out(priority_encoder_2_out));  // open: gs, en_out, en_in
  Register #(.width(4), .trigger("falling")) register_1 (
    .D(multiplexer_2_out), .en(multiplexer_3_out[0]), .Q(register_1_q), .clk(sc_1_out_6), .clr(in_1));
  Register #(.width(4), .trigger("falling")) register_2 (
    .D(multiplexer_2_out), .en(multiplexer_3_out[1]), .Q(register_2_q), .clk(sc_1_out_6), .clr(in_1));
  Register #(.width(4), .trigger("falling")) register_3 (
    .D(multiplexer_2_out), .en(multiplexer_3_out[2]), .Q(register_3_q), .clk(sc_1_out_6), .clr(in_1));
  Register #(.width(4)) register_4 (
    .D(multiplexer_2_out), .en(multiplexer_3_out[3]), .Q(register_4_q), .clk(sc_1_out_6), .clr(in_1));
  compare compare_1 (.in_1(multiplexer_2_out), .out_2(compare_1_out_2));
  Register #(.width(2)) register_5 (
    .D(compare_1_out_2), .en(dec_1_grzero), .Q(register_5_q), .clk(sc_1_out_6), .clr(in_1));
  OUTple outple_1 (
    .IN1(register_1_q), .IN2(register_2_q), .IN3(register_3_q), .IN4(register_4_q),
    .IN1sel(priority_encoder_1_out), .INT2sel(priority_encoder_2_out), .sel0(dec_1_addzero),
    .out_8(outple_1_out_8), .out_9(outple_1_out_9));
  ALU alu_1 (.in_1(outple_1_out_8), .in_2(outple_1_out_9), .out_3(alu_1_out_3));
endmodule

module SC (
  input  CLK,
  input  RST,
  output out_3,
  output out_4,
  output out_5,
  output out_6
);

  wire [1:0] counter_1_q;

  Counter #(.width(2), .max('h3)) counter_1 (
    .load(1'b0), .count(1'b1), .Q(counter_1_q), .clk(CLK), .clr(RST));  // open: D, carry
  Decoder #(.select(2), .enable("false")) decoder_1 (
    .out0(out_3), .out1(out_4), .out2(out_5), .out3(out_6), .sel(counter_1_q));
endmodule

module ALU (
  input  [3:0] in_1,
  input  [3:0] in_2,
  output [3:0] out_3
);

  Adder #(.width(4)) adder_1 (.a(in_1), .b(in_2), .out(out_3), .cin(1'b0));  // open: cout
endmodule

module compare (
  input  [3:0] in_1,
  output [1:0] out_2
);

  wire not_1_out, or_1_out;

  not not_1 (not_1_out, or_1_out);
  or or_1 (or_1_out, in_1[0], in_1[1], in_1[2], in_1[3]);
  Priority_Encoder #(.select(2)) priority_encoder_1 (
    .in1(in_1[0]), .in2(not_1_out), .out(out_2));  // open: in0, in3, gs, en_out, en_in
endmodule

module OUTple (
  input  [3:0] IN1,
  input  [3:0] IN2,
  input  [3:0] IN3,
  input  [3:0] IN4,
  input  [1:0] IN1sel,
  input  [1:0] INT2sel,
  input  sel0,
  output [3:0] out_8,
  output [3:0] out_9
);

  wire [3:0] multiplexer_2_out;

  Multiplexer #(.select(2), .width(4), .enable("false")) multiplexer_1 (
    .in0(IN1), .in1(IN2), .in2(IN3), .in3(IN4), .out(out_8), .sel(IN1sel));
  Multiplexer #(.select(2), .width(4), .enable("false")) multiplexer_2 (
    .in0(IN1), .in1(IN2), .in2(IN3), .in3(IN4), .out(multiplexer_2_out), .sel(INT2sel));
  Multiplexer #(.width(4), .enable("false")) multiplexer_3 (
    .in0(multiplexer_2_out), .in1(4'b0000), .out(out_9), .sel(sel0));
endmodule

module dec (
  input  [3:0] in_1,
  output sine,
  output zero,
  output INple,
  output addZERO,
  output GRZERO,
  output MEMlb,
  output refMEM
);

  wire and_4_out, and_5_out, and_6_out, and_7_out, and_9_out, and_10_out, and_11_out, not_1_out, not_2_out,
       not_3_out, not_4_out, not_5_out, not_6_out, not_7_out, not_8_out, not_9_out, not_10_out, not_11_out,
       not_12_out, not_13_out, not_14_out;

  and and_1 (sine, in_1[2], in_1[1]);
  and and_2 (zero, in_1[2], in_1[0]);
  not not_1 (not_1_out, in_1[1]);
  not not_2 (not_2_out, in_1[0]);
  not not_3 (not_3_out, in_1[2]);
  not not_4 (not_4_out, in_1[1]);
  not not_5 (not_5_out, in_1[2]);
  not not_6 (not_6_out, in_1[0]);
  not not_7 (not_7_out, in_1[2]);
  not not_8 (not_8_out, in_1[0]);
  not not_9 (not_9_out, in_1[2]);
  not not_10 (not_10_out, in_1[1]);
  not not_11 (not_11_out, in_1[2]);
  not not_12 (not_12_out, in_1[0]);
  not not_13 (not_13_out, in_1[1]);
  not not_14 (not_14_out, in_1[0]);
  and and_3 (refMEM, in_1[1], in_1[0]);
  and and_4 (and_4_out, in_1[1], in_1[0]);
  and and_5 (and_5_out, in_1[2], not_1_out, not_2_out);
  and and_6 (and_6_out, not_3_out, not_4_out, in_1[0]);
  and and_7 (and_7_out, not_5_out, in_1[1], not_6_out);
  and and_8 (GRZERO, not_7_out, in_1[1], not_8_out);
  and and_9 (and_9_out, not_9_out, not_10_out, in_1[0]);
  and and_10 (and_10_out, not_11_out, in_1[1], not_12_out);
  and and_11 (and_11_out, in_1[2], not_13_out, not_14_out);
  or or_1 (INple, and_4_out, and_5_out);
  or or_2 (addZERO, and_6_out, and_7_out);
  or or_3 (MEMlb, and_9_out, and_10_out, and_11_out);
endmodule
